# Fritzing sketch valveController (saved by Fritzing 0.9.3b)
breadboards: 1

parts:
  LED1 = LED - 5mm [color="Red (633nm)" package="5 mm [THT]"]
  LED_Blinker = Arduino Uno (Rev3)
  R1 = Resistor [tolerance=±5% resistance=560 package=THT]

nets:
  N1: LED1.cathode, R1.Pin_0
  N2: LED1.anode, LED_Blinker.D13/SCK
  N3: LED_Blinker.GND, R1.Pin_1

// code stored in the sketch: vlvctl.ino


int _ledPin = 13;


void setup() {
  // put your setup code here, to run once:
  pinMode(_ledPin, OUTPUT);

}


void loop() {
  // put your main code here, to run repeatedly:

  digitalWrite(_ledPin, HIGH);
  delay(100);
  digitalWrite(_ledPin, LOW);
  delay(100);  
}
